# Fritzing sketch layout (saved by Fritzing 0.9.3b)
breadboards: 1

parts:
  R1 = Resistor [tolerance=±5% resistance=220 package=THT]
  R2 = Resistor [tolerance=±5% resistance=220 package=THT]
  R3 = Resistor [tolerance=±5% resistance=220 package=THT]
  R4 = Resistor [tolerance=±5% resistance=220 package=THT]
  LED1 = LED - 5mm [color="Green (555nm)" package="5 mm [THT]"]
  LED2 = LED - 5mm [color="Blue (430nm)" package="5 mm [THT]"]
  LED3 = LED - 5mm [color="Yellow (585nm)" package="5 mm [THT]"]
  LED4 = LED - 5mm [color="Red (633nm)" package="5 mm [THT]"]
  Raspberry_Pi_1 = Raspberry Pi 3 [part_number=RPI-3-V1.2]
  Part1 = songle relay
  L1 = Solenoid
  Power_plug1 = Power plug
  RHT1 = Humidity and Temperature Sensor RHT03

nets:
  N1: R1.Pin_0, LED1.anode
  N2: R2.Pin_0, LED2.anode
  N3: R3.Pin_0, LED3.anode
  N4: R4.Pin_0, LED4.anode
  N5: LED1.cathode, Raspberry_Pi_1.GPIO2, Raspberry_Pi_1.GPIO26, Raspberry_Pi_1.GND, Raspberry_Pi_1.GPIO14, RHT1.GND_1
  N6: LED2.cathode, Raspberry_Pi_1.GPIO19
  N7: LED3.cathode, Raspberry_Pi_1.GPIO21
  N8: LED4.cathode, Raspberry_Pi_1.GPIO20
  N9: Raspberry_Pi_1.GPIO16, Part1.COMMON
  N10: Raspberry_Pi_1.GPIO18, RHT1.Data-signal
  5V: Raspberry_Pi_1.5V, RHT1.Vcc
  N11: Part1.NO, L1.pin2
  N12: Part1.NC, Power_plug1.GND
  N13: L1.pin1, Power_plug1.VCC
